// Logisim project segA.circ as structural Verilog: 9 circuits, main circuit main
module main (
);

  wire bcd_2_7seg_1_a, bcd_2_7seg_1_b, bcd_2_7seg_1_c, bcd_2_7seg_1_d, bcd_2_7seg_1_e, bcd_2_7seg_1_f,
       bcd_2_7seg_1_g, switch_1_p2, switch_2_p2, switch_3_p2, switch_4_p2;

  // Switch switch_1: pin names not known; wires that end beside it: 1'b1, switch_1_p2
  // Switch switch_2: pin names not known; wires that end beside it: 1'b1, switch_2_p2
  // Switch switch_3: pin names not known; wires that end beside it: 1'b1, switch_3_p2
  // Switch switch_4: pin names not known; wires that end beside it: 1'b1, switch_4_p2
  Pull_Resistor pull_resistor_1 (.node(switch_4_p2));
  Pull_Resistor pull_resistor_2 (.node(switch_3_p2));
  Pull_Resistor pull_resistor_3 (.node(switch_2_p2));
  Pull_Resistor pull_resistor_4 (.node(switch_1_p2));
  bcd_2_7seg bcd_2_7seg_1 (
    .i1(switch_4_p2), .i2(switch_3_p2), .i4(switch_2_p2), .i8(switch_1_p2), .a(bcd_2_7seg_1_a),
    .b(bcd_2_7seg_1_b), .c(bcd_2_7seg_1_c), .d(bcd_2_7seg_1_d), .e(bcd_2_7seg_1_e), .f(bcd_2_7seg_1_f),
    .g(bcd_2_7seg_1_g));
  _7_Segment_Display u_7_segment_display_1 (
    .g(bcd_2_7seg_1_g), .f(bcd_2_7seg_1_f), .a(bcd_2_7seg_1_a), .b(bcd_2_7seg_1_b), .e(bcd_2_7seg_1_e),
    .d(bcd_2_7seg_1_d), .c(bcd_2_7seg_1_c));  // open: dp
endmodule

module SEG_A (
  input  A,
  input  B,
  input  C,
  input  D,
  output segA
);

  wire and_1_out, nor_1_out, or_1_out, or_2_out, or_3_out;

  and and_1 (and_1_out, A, C);
  or or_1 (or_1_out, B, D);
  or or_2 (or_2_out, C, A);
  nor nor_1 (nor_1_out, or_2_out, D);
  or or_3 (or_3_out, and_1_out, nor_1_out);
  or or_4 (segA, or_3_out, or_1_out);

  // Notes on the sheet:
  //   A: pull=down
  //   B: pull=down
  //   C: pull=down
  //   D: pull=down
endmodule

module SEG_B (
  input  A,
  input  B,
  input  C,
  input  D,
  output segB
);

  wire and_1_out, and_2_out, not_1_out, not_2_out, not_3_out, or_1_out, or_2_out;

  not not_1 (not_1_out, A);
  not not_2 (not_2_out, B);
  not not_3 (not_3_out, C);
  and and_1 (and_1_out, A, B);
  and and_2 (and_2_out, not_1_out, not_2_out);
  or or_1 (or_1_out, not_3_out, D);
  or or_2 (or_2_out, and_1_out, and_2_out);
  or or_3 (segB, or_2_out, or_1_out);
endmodule

module SEG_C (
  input  A,
  input  B,
  input  C,
  input  D,
  output segC
);

  wire not_1_out, or_1_out, or_2_out;

  not not_1 (not_1_out, B);
  or or_1 (or_1_out, A, not_1_out);
  or or_2 (or_2_out, C, D);
  or or_3 (segC, or_1_out, or_2_out);
endmodule

module SEG_D (
  input  A,
  input  B,
  input  C,
  input  D,
  output segD
);

  wire and_1_out, and_2_out, and_3_out, and_4_out, and_5_out, and_6_out, not_1_out, not_2_out, not_3_out,
       not_4_out, or_1_out, or_2_out, or_3_out;

  not not_1 (not_1_out, A);
  not not_2 (not_2_out, B);
  not not_3 (not_3_out, C);
  not not_4 (not_4_out, D);
  and and_1 (and_1_out, B, not_3_out);
  and and_2 (and_2_out, not_1_out, not_2_out);
  and and_3 (and_3_out, and_2_out, not_3_out);
  and and_4 (and_4_out, not_2_out, and_5_out);
  and and_5 (and_5_out, A, C);
  and and_6 (and_6_out, B, not_1_out);
  or or_1 (or_1_out, and_3_out, and_4_out);
  or or_2 (or_2_out, D, and_6_out);
  or or_3 (or_3_out, or_1_out, or_2_out);
  or or_4 (segD, or_3_out, and_1_out);
endmodule

module SEG_E (
  input  A,
  input  B,
  input  C,
  input  D,
  output segE
);

  wire and_1_out, and_2_out, not_1_out, not_2_out;

  not not_1 (not_1_out, A);
  not not_2 (not_2_out, C);
  and and_1 (and_1_out, not_1_out, B);
  and and_2 (and_2_out, not_1_out, not_2_out);
  or or_1 (segE, and_1_out, and_2_out);
endmodule

module SEG_F (
  input  A,
  input  B,
  input  C,
  input  D,
  output segF
);

  wire and_1_out, and_2_out, and_3_out, not_1_out, not_2_out, or_1_out, or_2_out;

  not not_1 (not_1_out, A);
  not not_2 (not_2_out, B);
  and and_1 (and_1_out, C, not_1_out);
  and and_2 (and_2_out, not_1_out, not_2_out);
  and and_3 (and_3_out, not_2_out, C);
  or or_1 (or_1_out, and_2_out, D);
  or or_2 (or_2_out, and_1_out, and_3_out);
  or or_3 (segF, or_2_out, or_1_out);
endmodule

module SEG_G (
  input  A,
  input  B,
  input  C,
  input  D,
  output segG
);

  wire and_1_out, not_1_out, or_1_out, xor_1_out;

  not not_1 (not_1_out, A);
  and and_1 (and_1_out, not_1_out, B);
  xor xor_1 (xor_1_out, B, C);
  or or_1 (or_1_out, and_1_out, D);
  or or_2 (segG, or_1_out, xor_1_out);
endmodule

module bcd_2_7seg (
  input  i1,
  input  i2,
  input  i4,
  input  i8,
  output a,
  output b,
  output c,
  output d,
  output e,
  output f,
  output g
);

  SEG_A seg_a_1 (.A(i1), .B(i2), .C(i4), .D(i8), .segA(a));
  SEG_B seg_b_1 (.A(i1), .B(i2), .C(i4), .D(i8), .segB(b));
  SEG_C seg_c_1 (.A(i1), .B(i2), .C(i4), .D(i8), .segC(c));
  SEG_D seg_d_1 (.A(i1), .B(i2), .C(i4), .D(i8), .segD(d));
  SEG_E seg_e_1 (.A(i1), .B(i2), .C(i4), .D(i8), .segE(e));
  SEG_F seg_f_1 (.A(i1), .B(i2), .C(i4), .D(i8), .segF(f));
  SEG_G seg_g_1 (.A(i1), .B(i2), .C(i4), .D(i8), .segG(g));
endmodule
